// Logisim project comp-273-ass2.circ as structural Verilog: 2 circuits, main circuit main
module main (
  input  in_1,
  input  [3:0] Data,
  input  [1:0] Address,
  output [3:0] Output
);

  wire and_1_out, and_2_out, and_3_out, and_4_out, clock_1_out, d_ff_1_q, d_ff_2_q, d_ff_3_q, d_ff_4_q,
       d_ff_5_q, d_ff_6_q, d_ff_7_q, d_ff_8_q, d_ff_9_q, d_ff_10_q, d_ff_11_q, d_ff_12_q, d_ff_13_q,
       d_ff_14_q, d_ff_15_q, d_ff_16_q, d_ff_17_q, d_ff_18_q, d_ff_19_q, not_1_out, not_2_out, not_3_out,
       not_4_out, or_2_out, or_3_out, or_5_out, or_6_out, or_8_out, or_9_out, or_11_out, or_12_out,
       write_gate_2_out, write_gate_3_out, write_gate_4_out, write_gate_out;
  wire [3:0] Data_Register_output_1, or_1_out;

  D_Flip_Flop d_ff_1 (.clk(clock_1_out), .D(Address[0]), .Q(d_ff_1_q));  // open: Qn, preset, en, reset
  D_Flip_Flop d_ff_2 (.clk(clock_1_out), .D(Address[1]), .Q(d_ff_2_q));  // open: Qn, preset, en, reset
  not not_1 (not_1_out, d_ff_1_q);
  not not_2 (not_2_out, d_ff_2_q);
  not not_3 (not_3_out, d_ff_1_q);
  and and_1 (and_1_out, d_ff_1_q, not_4_out);
  not not_4 (not_4_out, d_ff_2_q);
  and and_2 (and_2_out, d_ff_1_q, d_ff_2_q);
  and and_3 (and_3_out, not_1_out, not_2_out);
  and write_gate (write_gate_out, and_3_out, d_ff_5_q);
  and and_4 (and_4_out, not_3_out, d_ff_2_q);
  and write_gate_2 (write_gate_2_out, and_4_out, d_ff_5_q);
  and write_gate_3 (write_gate_3_out, and_1_out, d_ff_5_q);
  and write_gate_4 (write_gate_4_out, d_ff_5_q, and_2_out);
  D_Flip_Flop d_ff_3 (
    .clk(clock_1_out), .D(Data_Register_output_1[3]), .Q(d_ff_3_q), .en(write_gate_2_out));  // open: Qn, preset, reset
  D_Flip_Flop d_ff_4 (
    .clk(clock_1_out), .D(Data_Register_output_1[3]), .Q(d_ff_4_q), .en(write_gate_3_out));  // open: Qn, preset, reset
  D_Flip_Flop d_ff_5 (.clk(clock_1_out), .D(in_1), .Q(d_ff_5_q));  // open: Qn, preset, en, reset
  Data_register Data_Register (
    .Output_1(Data_Register_output_1), .Input_1(Data), .Mode(d_ff_5_q), .Clock(clock_1_out),
    .Input_2(or_1_out), .Output_2(Output));
  D_Flip_Flop d_ff_6 (
    .clk(clock_1_out), .D(Data_Register_output_1[3]), .Q(d_ff_6_q), .en(write_gate_out));  // open: Qn, preset, reset
  D_Flip_Flop d_ff_7 (
    .clk(clock_1_out), .D(Data_Register_output_1[3]), .Q(d_ff_7_q), .en(write_gate_4_out));  // open: Qn, preset, reset
  Clock clock_1 (.out(clock_1_out));
  D_Flip_Flop d_ff_8 (
    .clk(clock_1_out), .D(Data_Register_output_1[2]), .Q(d_ff_8_q), .en(write_gate_out));  // open: Qn, preset, reset
  D_Flip_Flop d_ff_9 (
    .clk(clock_1_out), .D(Data_Register_output_1[2]), .Q(d_ff_9_q), .en(write_gate_2_out));  // open: Qn, preset, reset
  D_Flip_Flop d_ff_10 (
    .clk(clock_1_out), .D(Data_Register_output_1[2]), .Q(d_ff_10_q), .en(write_gate_3_out));  // open: Qn, preset, reset
  D_Flip_Flop d_ff_11 (
    .clk(clock_1_out), .D(Data_Register_output_1[2]), .Q(d_ff_11_q), .en(write_gate_4_out));  // open: Qn, preset, reset
  D_Flip_Flop d_ff_12 (
    .clk(clock_1_out), .D(Data_Register_output_1[1]), .Q(d_ff_12_q), .en(write_gate_out));  // open: Qn, preset, reset
  D_Flip_Flop d_ff_13 (
    .clk(clock_1_out), .D(Data_Register_output_1[1]), .Q(d_ff_13_q), .en(write_gate_2_out));  // open: Qn, preset, reset
  D_Flip_Flop d_ff_14 (
    .clk(clock_1_out), .D(Data_Register_output_1[1]), .Q(d_ff_14_q), .en(write_gate_3_out));  // open: Qn, preset, reset
  D_Flip_Flop d_ff_15 (
    .clk(clock_1_out), .D(Data_Register_output_1[1]), .Q(d_ff_15_q), .en(write_gate_4_out));  // open: Qn, preset, reset
  D_Flip_Flop d_ff_16 (
    .clk(clock_1_out), .D(Data_Register_output_1[0]), .Q(d_ff_16_q), .en(write_gate_out));  // open: Qn, preset, reset
  D_Flip_Flop d_ff_17 (
    .clk(clock_1_out), .D(Data_Register_output_1[0]), .Q(d_ff_17_q), .en(write_gate_2_out));  // open: Qn, preset, reset
  D_Flip_Flop d_ff_18 (
    .clk(clock_1_out), .D(Data_Register_output_1[0]), .Q(d_ff_18_q), .en(write_gate_3_out));  // open: Qn, preset, reset
  D_Flip_Flop d_ff_19 (
    .clk(clock_1_out), .D(Data_Register_output_1[0]), .Q(d_ff_19_q), .en(write_gate_4_out));  // open: Qn, preset, reset
  or or_1 (or_1_out[0], d_ff_16_q, or_2_out);
  or or_2 (or_2_out, d_ff_17_q, or_3_out);
  or or_3 (or_3_out, d_ff_18_q, d_ff_19_q);
  or or_4 (or_1_out[1], d_ff_12_q, or_5_out);
  or or_5 (or_5_out, d_ff_13_q, or_6_out);
  or or_6 (or_6_out, d_ff_14_q, d_ff_15_q);
  or or_7 (or_1_out[2], d_ff_8_q, or_8_out);
  or or_8 (or_8_out, d_ff_9_q, or_9_out);
  or or_9 (or_9_out, d_ff_10_q, d_ff_11_q);
  or or_10 (or_1_out[3], d_ff_6_q, or_11_out);
  or or_11 (or_11_out, d_ff_3_q, or_12_out);
  or or_12 (or_12_out, d_ff_4_q, d_ff_7_q);

  // Notes on the sheet:
  //   Mode (1=write,0=read)
  //   Clock
  //   you need 2 ticks to change written info to output after putting in read
  //   DO NOT MOVE the inputs, outputs or clock, Anything else can be moved.
endmodule

module Data_register (
  input  [3:0] Input_1,
  input  Mode,
  input  Clock,
  input  [3:0] Input_2,
  output [3:0] Output_1,
  output [3:0] Output_2
);

  wire and_1_out, and_2_out, and_3_out, and_4_out, and_5_out, and_6_out, and_7_out, and_8_out, not_1_out,
       not_2_out, not_3_out, not_4_out;

  not not_1 (not_1_out, Mode);
  not not_2 (not_2_out, Mode);
  not not_3 (not_3_out, Mode);
  not not_4 (not_4_out, Mode);
  and and_1 (and_1_out, Input_1[0], Mode);
  and and_2 (and_2_out, Input_1[1], Mode);
  and and_3 (and_3_out, Input_1[2], Mode);
  and and_4 (and_4_out, Input_1[3], Mode);
  and and_5 (and_5_out, Input_2[0], not_1_out);
  and and_6 (and_6_out, Input_2[1], not_2_out);
  and and_7 (and_7_out, Input_2[2], not_3_out);
  and and_8 (and_8_out, not_4_out, Input_2[3], Input_2[3]);
  D_Flip_Flop d_ff_1 (.clk(Clock), .D(and_1_out), .Q(Output_1[0]));  // open: Qn, preset, en, reset
  D_Flip_Flop d_ff_2 (.clk(Clock), .D(and_2_out), .Q(Output_1[1]));  // open: Qn, preset, en, reset
  D_Flip_Flop d_ff_3 (.clk(Clock), .D(and_3_out), .Q(Output_1[2]));  // open: Qn, preset, en, reset
  D_Flip_Flop d_ff_4 (.clk(Clock), .D(and_4_out), .Q(Output_1[3]));  // open: Qn, preset, en, reset
  D_Flip_Flop d_ff_5 (.clk(Clock), .D(and_5_out), .Q(Output_2[0]));  // open: Qn, preset, en, reset
  D_Flip_Flop d_ff_6 (.clk(Clock), .D(and_6_out), .Q(Output_2[1]));  // open: Qn, preset, en, reset
  D_Flip_Flop d_ff_7 (.clk(Clock), .D(and_7_out), .Q(Output_2[2]));  // open: Qn, preset, en, reset
  D_Flip_Flop d_ff_8 (.clk(Clock), .D(and_8_out), .Q(Output_2[3]));  // open: Qn, preset, en, reset

  // Notes on the sheet:
  //   when the mode is 0 then whatever is in register should be sent out to output
  //   the input should be sent as output to the nibbles, saving the data to be written and goes as output 1
endmodule
